# Fritzing sketch arucam (saved by Fritzing 0.9.2b)
breadboards: 1

parts:
  Raspberry_Pi1 = Raspberry Pi 2

nets:
  N1: Raspberry_Pi1.3v3, Raspberry_Pi1.GPIO2
  N2: Raspberry_Pi1.GPIO14, Raspberry_Pi1.GND

notes:
  3.3V
  Ground
  SCL
  SDATA
  VSYNC
  HREF
  PCLK
  XCLK
